# Fritzing sketch Solar_LED_Circuit_Sketch_Full (saved by Fritzing 0.9.5d)

parts:
  Part1 = TPS63020 power supply module
  M1 = DOIT Esp32 DevKit v1 (30 pins long, 11 pins width) [part_number=ESP32S-PIN30]
  M2 = RioRand LM2596
  VCC1 = 4 x AAA Battery Mount
  J2 = screw terminal, 6 pins
  Part2 = Solar Panel [package="Renogy 50 Watts 12 Volt Monocrystalline Bendable Solar Panel"]
  D1 = Zener Diode [part_number=1N4732A breakdown_voltage=3.6V package="300 mil [THT]"]
  A2 = circuit breaker C120N-1P
  INA1 = INA219 DC Current Sensor Breakout
  F1 = Fan - Ventilador [package=THT]
  R7 = Resistor [tolerance=±5% resistance=220 package="0402 [SMD]"]  # not connected
  R8 = Resistor [tolerance=±5% resistance=10k package="0402 [SMD]"]  # not connected
  D5 = Zener Diode [part_number=1N4732A breakdown_voltage=3.6V package="300 mil [THT]"]  # not connected
  R9 = Resistor [tolerance=±5% resistance=4.7 package="0402 [SMD]"]
  ZS-042_RTC1 = ZS-042 RTC Module
  DS1 = DS18B20 1-Wire Temperature Sensor Probe Cable
  LED2 = LEDs [package=led10mm]  # not connected
  Q1 = Basic FET N-Channel [package="D2Pak [SMD]"]
  D6 = LTE-302 [package=lte-302]
  R10 = Resistor [tolerance=±5% resistance=100 package="0402 [SMD]"]

nets:
  GND: Part1.GND_P2_1, M1.GND, INA1.GND, ZS-042_RTC1.GND
  N1: Part1.VIN_2, J2.pin5, A2.Pin_1
  3V3: M1.3V3, ZS-042_RTC1.VCC
  N2: M1.D4, DS1.shield
  N3: M1.D18, R10.Pin_1
  N4: M1.D21, INA1.SDA, ZS-042_RTC1.SDA
  N5: M1.D22, INA1.SCL, ZS-042_RTC1.SCL
  N6: M2.Pin_1, D1.cathode
  N7: M2.Pin_2, J2.pin2, Part2.Connector_2
  N8: M2.Pin_4, VCC1.-, J2.pin4
  N9: VCC1.+, A2.Pin_2
  N10: J2.pin1, Part2.Connector_1, D1.anode
  N11: F1.GND, Q1.drain
  N12: R9.Pin_1, DS1.VDD
  N13: D6.A, R10.Pin_0

notes:
  CC/CV Buck Coverter
  25A 600W
  Solar Panel Mono 18V 80W
  Battery
  32140 x 4 = 60A
  (Included BMS)
  Diode 10SQ050
  Terminal Block TB1506
  DC Breaker
  1P 16A
  Line/Input
  Load/Output
  INA226 Module
  ESP32
  622 LED
  3.2v 300W
  TPS63020 (5v)
  VBus Line
  5v Fan
  R4.7 kOhm
  DS18B20
  Temp Sensor
  DS3231
  Clock Module
  Terminal Block
  1 = Solar +
  2 = Solar -
  3 = Batt +
  4 = Com GND
  5 = Load/Output
  Mosfet IRZ44N
  IR LED
  (940nm)
  R100 Ohm

custom parts:
  TPS63020 power supply module: TPS63020 is a power supply module (buck-boost) with a efficiency as high as 96%. Input voltage range is from 1.8V to 5.5V. Output voltage is set via R1 and R3, most modules have a output voltage of 5V configured as default. This corresponds to R1=110K and R3=1M. For a output voltage of 3.3V R1 has to be changed to 180K (R3 can be kept at 1M). The output current is up to 3A. Switches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
  DOIT Esp32 DevKit v1 (30 pins long, 11 pins width): The DOIT Esp32 DevKit v1 is one of the development board created by DOIT to evaluate the ESP-WROOM-32 module. It is based on the ESP32 microcontroller that boasts Wifi, Bluetooth, Ethernet and Low Power support all in a single chip. (vanepp) made breadboard work, adjusted pin numbering and labels and reduced size of schematic and cleaned up pcb. This chip is 30pins long (2 x15) and 11 pins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
  Solar Panel: Renogy 50 Watts 12 Volt Solar Panel
  circuit breaker C120N-1P: C120N - circuit breaker - 1P - 125A - C curve.
  INA219 DC Current Sensor Breakout: INA DC Current Sensor Breakout
  Fan - Ventilador: Ventilador de 2 pines, se encuentra comunmente en computadoras de escritorio
